# Fritzing sketch wiring-card_reader (saved by Fritzing 1.0.4)
breadboards: 1

parts:
  125_kHz_RFID_module1 = RDM6300
  Part1 = RFID-RC522-v3
  J1 = Raspberry Pi Header 40pin [package=THT]
  Part2 = LCD1602-I2C
  R1 = Resistor [tolerance=±5% resistance=1k package="2512 [SMD]"]
  R2 = Resistor [tolerance=±5% resistance=1k package="2512 [SMD]"]

nets:
  N1: 125_kHz_RFID_module1.TX, 125_kHz_RFID_module1.GND#66, R2.Pin_0
  GND: 125_kHz_RFID_module1.GND#60, Part1.GND, J1.GND, Part2.GND, R1.Pin_1
  5V: 125_kHz_RFID_module1.+5V#61, J1.5V, Part2.VCC
  N2: Part1.SDA, J1.IO8
  N3: Part1.SCK, J1.IO11
  N4: Part1.MOSI, J1.IO10
  N5: Part1.MISO, J1.IO9
  N6: Part1.RST, J1.IO25
  3.3V: Part1.3.3V, J1.3V3
  N7: J1.GPIO2, Part2.SDA
  N8: J1.IO3, Part2.SCL
  N9: J1.IO15, R1.Pin_0, R2.Pin_1

notes:
  to Antenna

custom parts:
  RDM6300: 125 kHz RFID module (serial interface)
  RFID-RC522-v3: A simple China made RFID-RC522 Reader (6x4 cm); do check the pin labels, as this is a MFRC522 based clone.
  Raspberry Pi Header 40pin: Raspberry Pi 40 pin header - for creating your own shields. (Mar 2020, bb: make breadboard friendly (.4in pin spacing) and add labels. Schematic add labels. PCB make oblong pins to allow routing traces between the pins.)
  LCD1602-I2C: A standard character display, usually with 2x16 characters. Comes in many colors with LCM1602 IIC attached.
